# Fritzing sketch sensor (saved by Fritzing 0.9.2b)
circuit board: 2.38109cm x 2.63397cm
breadboards: 1

parts:
  IC1 = IC, DIP package, 8 pins [chip_label=IC]
  RHT1 = Humidity and Temperature Sensor RHT03
  VCC1 = Battery
  R1 = Resistor [tolerance=±5% resistance=1k package=THT]
  RST = female pin header, 2 pins [form="♀ (female)"]
  R2 = Resistor [tolerance=±5% resistance=1k package=THT]
  LED1 = LED - 3mm [color="Red (633nm)" package="3 mm [THT]"]
  H1 = double row female pin header, 8 pins [form="♀ (female)"]

nets:
  N1: IC1.pin2, H1.pin1
  N2: IC1.pin3, RHT1.Data-signal
  N3: IC1.pin4, RHT1.GND_2, VCC1.-, R1.Pin_1, R2.Pin_1, H1.pin5
  N4: IC1.pin5, H1.pin7
  N5: IC1.pin6, RST.pin1, H1.pin6
  N6: IC1.pin7, H1.pin3
  N7: IC1.pin8, H1.pin4
  N8: RHT1.Vcc, H1.pin2
  N9: R1.Pin_0, LED1.cathode
  N10: RST.pin2, R2.Pin_0
  N11: LED1.anode, H1.pin8

notes:
  V0.1.0
